# Fritzing sketch D1MiniRF (saved by Fritzing 0.9.3b)
breadboards: 1

parts:
  U1 = mystery part, 3 pins [chip_label=?Receiver]
  U2 = mystery part, 4 pins [chip_label=Transmitter]
  WeMos_D1_Mini1 = WeMos D1 Mini  # not connected
  S1 = Momentary Switch [package=ksa_sealed_tac_switch]
  R1 = Resistor [tolerance=±5% resistance=10k package=THT]

nets:
  N1: U1.pin1, U2.pin1, R1.Pin_0
  N2: U1.pin2, U2.pin4, S1.1
  N3: S1.3, R1.Pin_1
